# Fritzing sketch esp32c3_fan_temp (saved by Fritzing 0.9.3b)
circuit board: 5.64444cm x 8.46667cm
breadboards: 1

parts:
  R1_Tacho = Resistor [tolerance=±5% power=0.25 resistance=2.2k package=THT]
  M1 = DC Motor
  DHT11 = Humidity and Temperature Sensor RHT03
  X1 = USB Connectors [package=usb-a-h]
  M2 = DC Motor
  M3 = DC Motor
  M4 = DC Motor
  ESP32c3_mini = Espruino Pico
  R1_Tacho1 = Resistor [tolerance=±5% power=0.25 resistance=2.2k package=THT]
  R1_Tacho2 = Resistor [tolerance=±5% power=0.25 resistance=2.2k package=THT]
  R1_Tacho3 = Resistor [tolerance=±5% power=0.25 resistance=2.2k package=THT]

nets:
  N1: R1_Tacho.Pin_0, DHT11.Vcc, ESP32c3_mini.3.3, R1_Tacho1.Pin_0, R1_Tacho2.Pin_0, R1_Tacho3.Pin_0
  Tacho3: R1_Tacho.Pin_1, ESP32c3_mini.A2
  5V: M1.pin_1, X1.VBUS, M2.pin_1, M3.pin_1, M4.pin_1, ESP32c3_mini.Vin
  N2: M1.pin_2, DHT11.GND_2, X1.GND, M2.pin_2, M3.pin_2, M4.pin_2
  N3: DHT11.Data-signal, ESP32c3_mini.B4
  PWM1: ESP32c3_mini.B14
  PWM2: ESP32c3_mini.B13
  PWM3: ESP32c3_mini.B10
  PWM4: ESP32c3_mini.B1
  Tacho4: ESP32c3_mini.A3, R1_Tacho1.Pin_1
  Tacho2: ESP32c3_mini.A1, R1_Tacho2.Pin_1
  Tacho1: ESP32c3_mini.A0, R1_Tacho3.Pin_1
